// Logisim project 4-bit-microprocessor-datapath.circ as structural Verilog: 2 circuits, main circuit main
module main (
  input  [1:0] SEL_A,
  input  [1:0] OPR,
  input  [1:0] SEL_B,
  input  [1:0] SEL_D,
  input  LOAD,
  input  [3:0] Manual_IN,
  output [3:0] out_7,
  output [3:0] out_8,
  output out_9,
  output [3:0] out_10,
  output [3:0] out_11,
  output [3:0] out_12
);

  wire clock_1_out, decoder_1_out0, decoder_1_out1, decoder_1_out2, decoder_1_out3, RST_out;
  wire [3:0] multiplexer_1_out, multiplexer_2_out, multiplexer_3_out;

  Clock clock_1 (.out(clock_1_out));
  Button RST (.out(RST_out));
  Decoder #(.enable("false"), .select(2)) decoder_1 (
    .out0(decoder_1_out0), .out1(decoder_1_out1), .out2(decoder_1_out2), .out3(decoder_1_out3), .sel(SEL_D));
  Multiplexer #(.width(4)) multiplexer_1 (.in0(out_8), .in1(Manual_IN), .out(multiplexer_1_out), .sel(LOAD));
  Register #(.width(4)) R1 (.D(multiplexer_1_out), .en(decoder_1_out0), .clk(clock_1_out), .Q(out_7), .clr(RST_out));
  Register #(.width(4)) R2 (.D(multiplexer_1_out), .en(decoder_1_out1), .clk(clock_1_out), .Q(out_10), .clr(RST_out));
  Register #(.width(4)) R3 (.D(multiplexer_1_out), .en(decoder_1_out2), .clk(clock_1_out), .Q(out_11), .clr(RST_out));
  Register #(.width(4)) R4 (.D(multiplexer_1_out), .en(decoder_1_out3), .clk(clock_1_out), .Q(out_12), .clr(RST_out));
  Hex_Digit_Display hex_digit_display_1 (.value(out_7));  // open: dp
  Hex_Digit_Display hex_digit_display_2 (.value(out_10));  // open: dp
  Hex_Digit_Display hex_digit_display_3 (.value(out_11));  // open: dp
  Hex_Digit_Display hex_digit_display_4 (.value(out_12));  // open: dp
  Multiplexer #(.select(2), .width(4)) multiplexer_2 (
    .in0(out_7), .in1(out_10), .in2(out_11), .in3(out_12), .out(multiplexer_2_out), .sel(SEL_A));
  Multiplexer #(.select(2), .width(4)) multiplexer_3 (
    .in0(out_7), .in1(out_10), .in2(out_11), .in3(out_12), .out(multiplexer_3_out), .sel(SEL_B));
  Hex_Digit_Display hex_digit_display_5 (.value(out_8));  // open: dp
  ALU alu_1 (.A(multiplexer_2_out), .B(multiplexer_3_out), .OPR(OPR), .ALU_OUT(out_8), .Z_F(out_9));
  LED ZERO (.in(out_9));

  // Notes on the sheet:
  //   Code:
  //   00: Addition
  //   01: Subtraction
  //   10: AND
  //   11: OR
endmodule

module ALU (
  input  [3:0] A,
  input  [3:0] B,
  input  [1:0] OPR,
  output [3:0] ALU_OUT,
  output Z_F
);

  wire [3:0] adder_1_out, and_1_out, or_1_out, subtractor_1_out;

  Adder #(.width(4)) adder_1 (.a(B), .b(A), .out(adder_1_out));  // open: cin, cout
  Subtractor #(.width(4)) subtractor_1 (.a(A), .b(B), .out(subtractor_1_out));  // open: bin, bout
  assign and_1_out = A & B;  // AND_Gate and_1, 4 bits wide
  assign or_1_out = A | B;  // OR_Gate or_1, 4 bits wide
  Multiplexer #(.select(2), .width(4)) multiplexer_1 (
    .in0(adder_1_out), .in1(subtractor_1_out), .in2(and_1_out), .in3(or_1_out), .out(ALU_OUT), .sel(OPR));
  nor nor_1 (Z_F, ALU_OUT[0], ALU_OUT[1], ALU_OUT[2], ALU_OUT[3]);
endmodule
